# Fritzing sketch diy-homekit-lights (saved by Fritzing 0.9.3b)
breadboards: 1

parts:
  Part1 = FadeCandy USB NeoPixel Driver [part_number=1689]
  MCU1 = Raspberry Pi Zero
  NEOPIXEL1 = Neopixel Strip -- White (60/m) [part_number=1138]
  JACK1 = 2.1mm DC Barrel Jack
  BUTTON1 = Waterproof Pushbutton (red)
  S1 = Round Pushbutton
  C1 = Electrolytic Capacitor [capacitance=4.7mF package="300 mil [THT, electrolytic]"]
  Part2 = Adafruit Micro USB Breakout [part_number="Adafruit #1833"]
  JP1 = USB_MICROB_PLUG [package=micro-b-ra-th]
  JP2 = USB_MICROB_PLUG [package=micro-b-ra-th]  # not connected

nets (from the schematic view):
  N1: Part1.GND, Part2.D-
  N2: Part1.D0, Part2.ID
  N3: MCU1.pin_6, MCU1.pin_30, MCU1.pin_39, BUTTON1.no_name_yet#5, S1.leg1
  N4: MCU1.pin_8, BUTTON1.no_name_yet#4
  N5: MCU1.pin_40, S1.leg0
  N6: NEOPIXEL1.GND#4, JP1.D-, JP1.GND
  N7: NEOPIXEL1.DO, JP1.ID
  N8: NEOPIXEL1.+5V#6, JP1.VCC
  N9: JACK1.center, BUTTON1.no_name_yet#1
  N10: JACK1.sleeve, C1.-, Part2.GND
  N11: BUTTON1.no_name_yet#2, C1.+, Part2.VBUS

notes:
  <-- power in
  USB OTG To FadeCandy
  micro USB Power to Pi
  USB From Pi
  Plug into NeoPixel Jack
  NeoPixel Jack
  On/Off Power Switch
  Graceful Shutdown Button
  DC Power Jack

custom parts:
  FadeCandy USB NeoPixel Driver: A new collaboration between Adafruit & Micah from Scanlime, we are excited to introduce Fadecandy, a NeoPixel driver with built in dithering, that can be controlled over USB. Fadecandy is not just hardware! It is a kit of both hardware and software parts that make LED art projects easier to build and better-looking.
  Neopixel Strip -- White (60/m): Neopixel Strip, White, 60 pixels per meter.
  2.1mm DC Barrel Jack: 2.1mm DC Barrel Jack with Thru-Hole Connectors (breadboardable)
  Waterproof Pushbutton (red): Waterproof Illuminated Pushbutton (red)
  Adafruit Micro USB Breakout: Simple but effective - this breakout board has a USB Micro-B connector, with all 5 pins broken out. Great for pairing with a microcontroller with USB support, or adding USB 5V power to a project. We use a micro-AB connector with through-hole shielding pads for an excellent strong connection - it won't rip off by accident! Comes with one fully assembled and tested micro B breakout PCB and a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
